# Fritzing sketch Motors (saved by Fritzing 0.9.10b)
circuit board: 8.46667cm x 5.64444cm
breadboards: 1

parts:
  Part1 = Arduino Uno (Rev3)
  LED1 = LED - 5mm [color="Red (633nm)" current=0.030 package="5 mm [THT]"]
  R1 = Resistor [tolerance=±5% power=0.25 resistance=220 package=THT]
  J1 = Dagu DGServo 9g header (male) [package=THT]
  J2 = Dagu DGServo 9g header (male) [package=THT]
  J3 = Dagu DGServo 9g header (male) [package=THT]
  J4 = Dagu DGServo 9g header (male) [package=THT]
  R2 = Rotary Potentiometer (Small) [maximum_resistance=100kΩ knob_status=50% power=0.5W package=THT]
  S1 = Pushbutton [package="[THT]"]

nets:
  N1: Part1.A0, R2.wiper
  N2: Part1.D8, J4.pulse
  N3: Part1.D9_PWM, J3.pulse
  N4: Part1.D10_PWM/SS, J2.pulse
  N5: Part1.D11_PWM/MOSI, J1.pulse
  N6: Part1.D2, S1.Pin_1, S1.Pin_2
  N7: Part1.D7, LED1.anode
  VCC: Part1.5V, J1.Vcc, J2.Vcc, J3.Vcc, J4.Vcc, R2.leg2
  GND: Part1.GND, J1.gnd, J2.gnd, J3.gnd, J4.gnd, R2.leg1, S1.Pin_3, S1.Pin_4
  N8: LED1.cathode, R1.Pin_0
