# Fritzing sketch nRF24L01-RX-Test (saved by Fritzing 0.9.10b)

parts:
  Part3 = NRF24L01+ Breakout Board
  Part4 = Arduino Nano (Rev3.0)

nets:
  GND: Part3.GND, Part4.GND
  VCC: Part3.VCC, Part4.5V
  N1: Part3.CE, Part4.D9
  N2: Part3.CS, Part4.D10
  N3: Part3.SCK, Part4.D13/SCK
  N4: Part3.MOSI, Part4.D11/MOSI
  N5: Part3.MISO, Part4.D12/MISO
