# Fritzing sketch nRF24L01-TX-Test (saved by Fritzing 0.9.10b)
breadboards: 1

parts:
  Part1 = Arduino Uno (Rev3)
  Part3 = NRF24L01+ Breakout Board
  S1 = Momentary Switch [package=ksa_sealed_tac_switch]
  S2 = Momentary Switch [package=ksa_sealed_tac_switch]
  S3 = Momentary Switch [package=ksa_sealed_tac_switch]
  R1 = Rotary Potentiometer (Small) [maximum_resistance=100kΩ knob_status=50% power=0.5W package=THT]

nets:
  N1: Part1.A0, R1.wiper
  N2: Part1.D9_PWM, Part3.CE
  N3: Part1.D10_PWM/SS, Part3.CS
  N4: Part1.D11_PWM/MOSI, Part3.MOSI
  N5: Part1.D12/MISO, Part3.MISO
  N6: Part1.D13/SCK, Part3.SCK
  N7: Part1.D4, S2.2
  N8: Part1.D5_PWM, S3.4
  N9: Part1.D6_PWM, S1.4
  5V: Part1.5V, Part3.VCC, R1.leg2
  GND: Part1.GND, Part3.GND, S1.2, S2.4, S3.2, R1.leg1
